// Logisim project SelfTask.circ as structural Verilog: 4 circuits, main circuit main
// AutoSchema
module main (
  input  [4:0] in_1
);

  wire [2:0] AutoSchema_out0, \Схема_Logic_Friday_out0 , \Схема_толька_на_элементах_И_НЕ_out0 ;

  // Probe on in_1
  AutoSchema AutoSchema (
    .in4(in_1[4]), .in3(in_1[3]), .in2(in_1[2]), .in1(in_1[1]), .in0(in_1[0]), .out2(AutoSchema_out0[2]),
    .out1(AutoSchema_out0[1]), .out0(AutoSchema_out0[0]));
  LogicFriday \u_Схема_Logic_Friday  (
    .in4(in_1[4]), .in3(in_1[3]), .in2(in_1[2]), .in1(in_1[1]), .in0(in_1[0]),
    .out1(\Схема_Logic_Friday_out0 [1]), .out0(\Схема_Logic_Friday_out0 [0]),
    .out2(\Схема_Logic_Friday_out0 [2]));
  SchemaAndNot \u_Схема_толька_на_элементах_И_НЕ  (
    .in4(in_1[4]), .in3(in_1[3]), .in2(in_1[2]), .in1(in_1[1]), .in0(in_1[0]),
    .out2(\Схема_толька_на_элементах_И_НЕ_out0 [2]), .out1(\Схема_толька_на_элементах_И_НЕ_out0 [1]),
    .out0(\Схема_толька_на_элементах_И_НЕ_out0 [0]));
  // Probe on AutoSchema_out0
  // Probe on \Схема_Logic_Friday_out0 
  // Probe on \Схема_толька_на_элементах_И_НЕ_out0 
endmodule

module AutoSchema (
  input  in4,
  input  in3,
  input  in2,
  input  in1,
  input  in0,
  output out2,
  output out1,
  output out0
);

  wire and_1_out, and_2_out, and_3_out, and_4_out, not_1_out, not_2_out, not_3_out, not_4_out, not_5_out;

  not not_1 (not_1_out, in4);
  not not_2 (not_2_out, in4);
  not not_3 (not_3_out, in4);
  not not_4 (not_4_out, in2);
  not not_5 (not_5_out, in4);
  and and_1 (and_1_out, not_1_out, in2);
  and and_2 (and_2_out, not_2_out, in3);
  and and_3 (and_3_out, not_3_out, not_4_out, in1);
  and and_4 (and_4_out, not_5_out, in3);
  or or_1 (out1, and_1_out, and_2_out);
  or or_2 (out0, and_3_out, and_4_out);

  assign out2 = in4;
endmodule

module SchemaAndNot (
  input  in4,
  input  in3,
  input  in2,
  input  in1,
  input  in0,
  output out2,
  output out1,
  output out0
);

  wire nand_1_out, nand_2_out, nand_3_out, nand_4_out, nand_5_out, nand_6_out, nand_7_out, nand_8_out,
       nand_9_out;

  nand nand_1 (nand_1_out, in4, in4);
  nand nand_2 (nand_2_out, in4, in4);
  nand nand_3 (nand_3_out, in4, in4);
  nand nand_4 (nand_4_out, in2, in2);
  nand nand_5 (nand_5_out, in4, in4);
  nand nand_6 (nand_6_out, nand_1_out, in2);
  nand nand_7 (nand_7_out, nand_2_out, in3);
  nand nand_8 (nand_8_out, nand_3_out, nand_4_out, in1);
  nand nand_9 (nand_9_out, nand_5_out, in3);
  nand nand_10 (out1, nand_6_out, nand_7_out);
  nand nand_11 (out0, nand_8_out, nand_9_out);

  assign out2 = in4;
endmodule

module LogicFriday (
  input  in4,
  input  in3,
  input  in2,
  input  in1,
  input  in0,
  output out1,
  output out0,
  output out2
);

  wire and_2_out, not_1_out, not_2_out, or_1_out, or_2_out;

  not not_1 (not_1_out, in4);
  not not_2 (not_2_out, in2);
  or or_1 (or_1_out, in2, in3);
  and and_1 (out1, not_1_out, or_1_out);
  and and_2 (and_2_out, in1, not_2_out);
  or or_2 (or_2_out, and_2_out, in3);
  and and_3 (out0, not_1_out, or_2_out);

  assign out2 = in4;
endmodule
