// Logisim project Task1.circ as structural Verilog: 2 circuits, main circuit main
module main (
  input  x,
  input  y,
  output out_3
);

  wire and_1_out, and_2_out, not_1_out, not_2_out;

  not not_1 (not_1_out, x);
  and and_1 (and_1_out, not_1_out, y);
  and and_2 (and_2_out, x, not_2_out);
  not not_2 (not_2_out, y);
  or or_1 (out_3, and_1_out, and_2_out);

  // Notes on the sheet:
  //   Моя схема
endmodule

module autoscheme (
  input  x,
  input  y,
  output \xor 
);

  wire and_1_out, and_2_out, not_1_out, not_2_out;

  not not_1 (not_1_out, x);
  not not_2 (not_2_out, y);
  and and_1 (and_1_out, not_1_out, y);
  and and_2 (and_2_out, x, not_2_out);
  or or_1 (\xor , and_1_out, and_2_out);

  // Notes on the sheet:
  //   Автоматически-построенная схема
endmodule
