// Logisim project Task2.circ as structural Verilog: 3 circuits, main circuit autoscheme
// AutoSchema
module autoscheme (
  input  in2,
  input  in1,
  input  in0,
  output f7,
  output f6,
  output f5,
  output f4,
  output f3,
  output f2,
  output f1,
  output f0
);

  wire and_6_out, and_7_out, not_1_out, not_2_out, not_3_out, not_4_out, not_5_out;

  and and_1 (f7, in2, in1, in0);
  and and_2 (f6, in2, in1, in0);
  and and_3 (f5, in2, in1);
  and and_4 (f4, in2, in1, in0);
  not not_1 (not_1_out, in1);
  not not_2 (not_2_out, in1);
  not not_3 (not_3_out, in0);
  not not_4 (not_4_out, in1);
  not not_5 (not_5_out, in0);
  and and_5 (f2, in2, not_1_out, in0);
  and and_6 (and_6_out, in2, not_2_out, in0);
  and and_7 (and_7_out, in2, in1, not_3_out);
  and and_8 (f0, in2, not_4_out, not_5_out);
  or or_1 (f1, and_6_out, and_7_out);

  assign f3 = 1'b0;
endmodule

// Logic Friday
module logic_friday (
  input  in2,
  input  in1,
  input  in0,
  output f6,
  output f2,
  output f7,
  output f1,
  output f5,
  output f4,
  output f3,
  output f0
);

  wire and_2_out, and_4_out, nand_1_out, not_1_out, not_2_out, not_3_out, or_1_out;

  not not_1 (not_1_out, in1);
  and and_1 (f5, in1, in2);
  not not_2 (not_2_out, in0);
  and and_2 (and_2_out, in0, in2, not_1_out);
  and and_3 (f0, not_2_out, not_1_out, in2);
  nand nand_1 (nand_1_out, not_2_out, f5);
  not not_3 (not_3_out, and_2_out);
  and and_4 (and_4_out, not_3_out, nand_1_out);
  or or_1 (or_1_out, and_4_out, f5);
  and and_5 (f4, and_4_out, f5);
  not not_4 (f1, and_4_out);
  not not_5 (f2, or_1_out);

  assign f3 = 1'b0;
  assign f6 = f4;
  assign f7 = f4;
endmodule

module main (
  input  [2:0] in_1
);

  wire [7:0] autoscheme_1_f0;
  wire [7:1] logic_friday_1_f1;

  // Probe on in_1
  logic_friday logic_friday_1 (
    .in2(in_1[2]), .in1(in_1[1]), .in0(in_1[0]), .f6(logic_friday_1_f1[6]), .f2(logic_friday_1_f1[2]),
    .f7(logic_friday_1_f1[7]), .f1(logic_friday_1_f1[1]), .f5(logic_friday_1_f1[5]),
    .f4(logic_friday_1_f1[4]), .f3(logic_friday_1_f1[4]), .f0(logic_friday_1_f1[4]));
  autoscheme autoscheme_1 (
    .in2(in_1[2]), .in1(in_1[1]), .in0(in_1[0]), .f7(autoscheme_1_f0[7]), .f6(autoscheme_1_f0[6]),
    .f5(autoscheme_1_f0[5]), .f4(autoscheme_1_f0[4]), .f3(autoscheme_1_f0[3]), .f2(autoscheme_1_f0[2]),
    .f1(autoscheme_1_f0[1]), .f0(autoscheme_1_f0[0]));
  // Probe on {logic_friday_1_f1[7:4], logic_friday_1_f1[4], logic_friday_1_f1[2:1], logic_friday_1_f1[4]}
  // Probe on autoscheme_1_f0
endmodule
